// Digital circuit bw8.dig as structural Verilog
module bw8 (
  input  Nmi,
  input  Irq,
  input  Req,
  input  _100_Hz,
  input  _1_Hz
);

  wire add_carry, and_7_out, and_8_out, AssertSystemBus, AsyncReset_out, carry, Clk, d_ff_as_1_q,
       d_ff_as_2_q, d_ff_as_3_q, EnableExtension, EnterKernelMode, Ext, JumpDecoder_d, left_shift_carry,
       left_sign, LoadA, LoadB, LoadBR, LoadC, LoadD, LoadFlags, LoadIR, LoadOffset, LoadPC_H, LoadPC_L,
       LoadSP_H, LoadSP_L, LoadTPtr_H, LoadTPtr_L, LoadTReg, LoadX_H, LoadX_L, LoadY_H, LoadY_L,
       multiplexer_12_out, nand_1_out, nand_2_out, nand_3_out, nCodeAccess, negative, NewIrqEnable,
       NewnKernel, NewNmiActive, NewUserData, nIOAccess, not_1_out, not_2_out, nUseFastClock_out,
       nUsePulseClock_out, nUseSlowClock_out, or_1_out, or_2_out, or_3_out, or_4_out, or_6_out,
       PointerWriteBackSelect, PowerOnReset_out, RegisterLoadEnable, RegisterWriteBackSelect, ResultSelect,
       right_shift_carry, Rst_t, Sequencer_ovf, SetNmiActive, Step_out, Write;
  wire [0:0] ClockMode_q;
  wire [1:0] AdderSelect, CarrySelect, ClockMode_q_2, Int, IrqEnableFlagControl, OffsetMode, or_5_out,
       PointerLoadEnable, priorityencoder_1_num, ShiftSelect, UserDataFlagControl;
  wire [1:1] InterruptLatch_q;
  wire [2:0] and_1_out, Control, JumpCondition, LeftSelect, mcr, multiplexer_4_out_2, PointerLoadSelect,
       PointerSelect, RegisterLoadSelect, RightSelect, Seq;
  wire [2:1] NewAluFlags;
  wire [3:0] AluFlags, AluFunction, and_4_out, Bank, br, Flags, LogicSelect, mbr, multiplexer_16_out;
  wire [4:0] and_5_out, and_6_out;
  wire [6:0] result, shift, SHL_out;
  wire [7:0] areg, ASR_out, breg, creg, DataBus, decoder_1_out_0, decoder_2_out_0, decoder_3_out_0, dreg, ir,
       \logic , mdi, mdo, MemoryData, multiplexer_1_out, multiplexer_2_out, multiplexer_5_out,
       multiplexer_8_out, multiplexer_9_out, multiplexer_13_out, multiplexer_15_out, multiplexer_19_out, off,
       temp;
  wire [7:1] SHR_out;
  wire [10:0] AluDecoder_d;
  wire [14:14] ControlLines_q;
  wire [15:0] add_2_s, Address, bitextender_1_out, mar, multiplexer_6_out, multiplexer_7_out, pc, sp, tp, xp,
       yp;
  wire [23:0] multiplexer_4_out;
  wire [40:0] InterruptDecoder_d, PrimaryDecoder_d;

  Decoder #(.Selector_Bits(3)) decoder_1 (
    .sel(PointerLoadSelect), .out_0(decoder_1_out_0[7]), .out_1(decoder_1_out_0[6]),
    .out_2(decoder_1_out_0[5]), .out_3(decoder_1_out_0[4]), .out_4(decoder_1_out_0[3]),
    .out_5(decoder_1_out_0[2]), .out_6(decoder_1_out_0[1]), .out_7(decoder_1_out_0[0]));
  Decoder #(.Selector_Bits(3)) decoder_2 (
    .sel(PointerLoadSelect), .out_0(decoder_2_out_0[0]), .out_1(decoder_2_out_0[1]),
    .out_2(decoder_2_out_0[2]), .out_3(decoder_2_out_0[3]), .out_4(decoder_2_out_0[4]),
    .out_5(decoder_2_out_0[5]), .out_6(decoder_2_out_0[6]), .out_7(decoder_2_out_0[7]));
  or or_1 (or_1_out, ControlLines_q[14], Rst_t);
  or or_2 (or_2_out, Sequencer_ovf, ControlLines_q[14]);
  reg8 InstructionRegister (.D(DataBus), .C(Clk), .en(LoadIR), .clr(Rst_t), .Q(ir));
  Multiplexer #(.Bits(8)) multiplexer_1 (
    .sel(PointerLoadEnable[1]), .in_0({8{1'b0}}), .in_1(decoder_1_out_0),
    .out({multiplexer_1_out[7:5], and_5_out[3:0], multiplexer_1_out[0]}));
  Multiplexer #(.Bits(8)) multiplexer_2 (
    .sel(PointerLoadEnable[0]), .in_0({8{1'b0}}), .in_1(decoder_2_out_0),
    .out({multiplexer_2_out[7:5], and_6_out[3:0], multiplexer_2_out[0]}));
  Button #(.activeLow("true")) nUseFastClock (.out(nUseFastClock_out));
  Button #(.activeLow("true")) nUseSlowClock (.out(nUseSlowClock_out));
  Button #(.activeLow("true")) nUsePulseClock (.out(nUsePulseClock_out));
  Reset #(.invertOutput("false")) PowerOnReset (.out(PowerOnReset_out));
  Button AsyncReset (.out(AsyncReset_out));
  Counter #(.Bits(3)) Sequencer (.en(1'b1), .C(Clk), .clr(or_1_out), .out(Seq), .ovf(Sequencer_ovf));
  RS_FF Extension_Bit (.S(EnableExtension), .C(Clk), .R(or_2_out), .Q(Ext));  // open: nQ
  D_FF #(.Bits(3)) InterruptLatch (
    .D({Nmi, Irq, Req}), .C(Clk), .Q({and_4_out[3], InterruptLatch_q[1], and_4_out[0]}));  // open: nQ
  nand nand_1 (nand_1_out, and_1_out[1], and_1_out[0]);
  nand nand_2 (nand_2_out, and_1_out[0], and_1_out[2]);
  nand nand_3 (nand_3_out, and_1_out[1], and_1_out[2]);
  or or_3 (or_3_out, PowerOnReset_out, AsyncReset_out);
  ROM #(.AddrBits(7)) JumpDecoder (.A({AluFlags, JumpCondition}), .sel(1'b1), .D(JumpDecoder_d));
  not not_1 (not_1_out, or_3_out);
  and and_1 (and_1_out[2], nand_1_out, 1'b1, nUseFastClock_out);
  and and_2 (and_1_out[1], nand_2_out, not_1_out, nUseSlowClock_out);
  and and_3 (and_1_out[0], 1'b1, nand_3_out, nUsePulseClock_out, 1'b1);
  D_FF_AS d_ff_as_1 (.Set(1'b0), .D(1'b1), .C(Clk), .Clr(or_3_out), .Q(d_ff_as_1_q));  // open: nQ
  ROM #(.AddrBits(12), .Bits(41)) PrimaryDecoder (.A({Ext, ir, Seq}), .sel(1'b1), .D(PrimaryDecoder_d));
  D_FF_AS #(.Bits(2)) InterruptMode (
    .Set(1'b0), .D(priorityencoder_1_num), .C(or_2_out), .Clr(Rst_t), .Q(Int));  // open: nQ
  and and_4 (and_4_out[1], Flags[0], InterruptLatch_q[1]);
  and and_5 (and_5_out[4], multiplexer_1_out[0], JumpDecoder_d);
  and and_6 (and_6_out[4], multiplexer_2_out[0], JumpDecoder_d);
  PriorityEncoder #(.Selector_Bits(2)) priorityencoder_1 (
    .in0(1'b0), .in1(and_4_out[3]), .in2(and_4_out[1]), .in3(and_4_out[0]), .num(priorityencoder_1_num));  // open: any
  // NotConnected on and_4_out[2]
  D_FF_AS d_ff_as_2 (.Set(1'b0), .D(d_ff_as_1_q), .C(Clk), .Clr(or_3_out), .Q(d_ff_as_2_q));  // open: nQ
  Button Step (.out(Step_out));
  ROM #(.AddrBits(5), .Bits(41)) InterruptDecoder (.A({Int, Seq}), .sel(1'b1), .D(InterruptDecoder_d));
  or or_4 (or_4_out, Int[0], Int[1]);
  D_FF_AS #(.Bits(5)) PointerControlLines__High (
    .Set(1'b0), .D(and_5_out), .C(Clk), .Clr(Rst_t), .Q({LoadPC_H, LoadSP_H, LoadX_H, LoadY_H, LoadTPtr_H}));  // open: nQ
  D_FF_AS #(.Bits(5)) PointerControlLines__Low (
    .Set(1'b0), .D(and_6_out), .C(Clk), .Clr(Rst_t), .Q({LoadPC_L, LoadSP_L, LoadX_L, LoadY_L, LoadTPtr_L}));  // open: nQ
  not not_2 (not_2_out, _100_Hz);
  D_FF #(.Bits(3)) ClockMode (
    .D(and_1_out), .C(_100_Hz), .Q({ClockMode_q_2[0], ClockMode_q_2[1], ClockMode_q[0]}));  // open: nQ
  D_FF_AS d_ff_as_3 (.Set(1'b0), .D(d_ff_as_2_q), .C(Clk), .Clr(or_3_out), .Q(d_ff_as_3_q));  // open: nQ
  Multiplexer #(.Selector_Bits(2)) multiplexer_3 (
    .sel(ClockMode_q_2), .in_0(Step_out), .in_1(_1_Hz), .in_2(not_2_out), .in_3(Step_out), .out(Clk));
  Multiplexer #(.Bits(41)) multiplexer_4 (
    .sel(or_4_out), .in_0(PrimaryDecoder_d), .in_1(InterruptDecoder_d),
    .out({PointerLoadEnable, PointerLoadSelect, JumpCondition, AluFunction, RegisterLoadSelect, RegisterLoadEnable, or_5_out[1], multiplexer_4_out[23:10], multiplexer_4_out_2, multiplexer_4_out[6:0]}));
  LED nFast (.in(ClockMode_q_2[0]));
  LED nSlow (.in(ClockMode_q_2[1]));
  LED nStep (.in(ClockMode_q[0]));
  not not_3 (Rst_t, d_ff_as_3_q);
  LED Clock (.in(Clk));
  Decoder #(.Selector_Bits(3)) decoder_3 (
    .sel(RegisterLoadSelect), .out_0(decoder_3_out_0[0]), .out_1(decoder_3_out_0[1]),
    .out_2(decoder_3_out_0[2]), .out_3(decoder_3_out_0[3]), .out_4(decoder_3_out_0[4]),
    .out_5(decoder_3_out_0[5]), .out_6(decoder_3_out_0[6]), .out_7(decoder_3_out_0[7]));
  or or_5 (or_5_out[0], multiplexer_4_out_2[2], multiplexer_4_out_2[1], multiplexer_4_out_2[0]);
  Multiplexer #(.Bits(8)) multiplexer_5 (
    .sel(RegisterLoadEnable), .in_0({8{1'b0}}), .in_1(decoder_3_out_0), .out(multiplexer_5_out));
  ROM #(.AddrBits(4), .Bits(11)) AluDecoder (.A(AluFunction), .sel(1'b1), .D(AluDecoder_d));
  LED led_1 (.in(Ext));
  // Probe Bank Address Register on mbr
  // Probe Address Register on mar
  // Probe Program Counter on pc
  // Probe Stack Pointer on sp
  // Probe X Pointer on xp
  // Probe Y Pointer on yp
  // Probe Temp Pointer on tp
  // Probe Bank Register on br
  // Probe Instruction Register on ir
  D_FF_AS #(.Bits(24)) ControlLines (
    .Set(1'b0), .D({multiplexer_4_out[23:10], multiplexer_4_out_2, multiplexer_4_out[6:0]}), .C(Clk),
    .Clr(Rst_t),
    .Q({Write, LoadFlags, EnterKernelMode, SetNmiActive, UserDataFlagControl, IrqEnableFlagControl, EnableExtension, ControlLines_q[14], AssertSystemBus, OffsetMode, PointerWriteBackSelect, PointerSelect, RegisterWriteBackSelect, RightSelect, LeftSelect}));  // open: nQ
  D_FF_AS #(.Bits(2)) BusControlLines (
    .Set(1'b0), .D(or_5_out), .C(Clk), .Clr(Rst_t), .Q({nIOAccess, nCodeAccess}));  // open: nQ
  D_FF_AS #(.Bits(8)) RegisterControlLines (
    .Set(1'b0), .D(multiplexer_5_out), .C(Clk), .Clr(Rst_t),
    .Q({LoadIR, LoadTReg, LoadBR, LoadOffset, LoadD, LoadC, LoadB, LoadA}));  // open: nQ
  D_FF_AS #(.Bits(11)) AluControlLines (
    .Set(1'b0), .D(AluDecoder_d), .C(Clk), .Clr(Rst_t),
    .Q({ResultSelect, CarrySelect, AdderSelect, LogicSelect, ShiftSelect}));  // open: nQ
  // Probe Memory Data Out on mdo
  // Probe Memory Data In on mdi
  // Probe A Register on areg
  // Probe B Register on breg
  // Probe C Register on creg
  // Probe D Register on dreg
  // Probe Temp Register on temp
  // Probe Offset Register on off
  LED u_Carry (.in(AluFlags[3]));
  LED Zero (.in(AluFlags[2]));
  LED Overflow (.in(AluFlags[1]));
  LED Sign (.in(AluFlags[0]));
  LED NmiActive (.in(Flags[3]));
  LED nKernel (.in(Flags[2]));
  LED UserData (.in(Flags[1]));
  LED IrqEnable (.in(Flags[0]));
  LED led_2 (.in(Seq[2]));
  LED led_3 (.in(Seq[1]));
  LED led_4 (.in(Seq[0]));
  LED led_5 (.in(Int[1]));
  LED led_6 (.in(Int[0]));
  reg16 Program_Counter_2 (.D(multiplexer_6_out), .C(Clk), .EnL(LoadPC_L), .EnH(LoadPC_H), .clr(Rst_t), .Q(pc));
  reg16 Stack_Pointer_2 (.D(multiplexer_6_out), .C(Clk), .EnL(LoadSP_L), .EnH(LoadSP_H), .clr(Rst_t), .Q(sp));
  reg16 X_Pointer_2 (.D(multiplexer_6_out), .C(Clk), .EnL(LoadX_L), .EnH(LoadX_H), .clr(Rst_t), .Q(xp));
  reg16 Y_Pointer_2 (.D(multiplexer_6_out), .C(Clk), .EnL(LoadY_L), .EnH(LoadY_H), .clr(Rst_t), .Q(yp));
  reg16 Temp_Pointer_2 (.D(multiplexer_6_out), .C(Clk), .EnL(LoadTPtr_L), .EnH(LoadTPtr_H), .clr(Rst_t), .Q(tp));
  reg8 GPR_A (.D(DataBus), .C(Clk), .en(LoadA), .clr(Rst_t), .Q(areg));
  reg8 GPR_B (.D(DataBus), .C(Clk), .en(LoadB), .clr(Rst_t), .Q(breg));
  reg8 GPR_C (.D(DataBus), .C(Clk), .en(LoadC), .clr(Rst_t), .Q(creg));
  reg8 GPR_D (.D(DataBus), .C(Clk), .en(LoadD), .clr(Rst_t), .Q(dreg));
  reg8 u_Temp (.D(DataBus), .C(Clk), .en(LoadTReg), .clr(Rst_t), .Q(temp));
  Multiplexer #(.Bits(16)) multiplexer_6 (
    .sel(PointerWriteBackSelect), .in_0({DataBus, DataBus}), .in_1(add_2_s), .out(multiplexer_6_out));
  Multiplexer #(.Selector_Bits(3), .Bits(16)) multiplexer_7 (
    .sel(PointerSelect), .in_0(pc), .in_1(sp), .in_2(xp), .in_3(yp), .in_4(tp), .in_5(16'h3), .in_6(16'h6),
    .in_7(16'h9), .out(multiplexer_7_out));
  Multiplexer #(.Selector_Bits(3), .Bits(8)) multiplexer_8 (
    .sel(LeftSelect), .in_0(areg), .in_1(breg), .in_2(creg), .in_3(dreg), .in_4(temp), .in_5({8{1'b0}}),
    .in_6({8{1'b0}}), .in_7({8{1'b0}}), .out(multiplexer_8_out));
  Multiplexer #(.Selector_Bits(3), .Bits(8)) multiplexer_9 (
    .sel(RightSelect), .in_0(areg), .in_1(breg), .in_2(creg), .in_3(dreg), .in_4(temp), .in_5({8{1'b0}}),
    .in_6({8{1'b0}}), .in_7({8{1'b0}}), .out(multiplexer_9_out));
  BarrelShifter #(.Bits(8)) SHL (.in(multiplexer_8_out), .shift(4'b0001), .out({left_shift_carry, SHL_out}));
  BarrelShifter #(.Bits(8), .direction("right")) SHR (
    .in(multiplexer_8_out), .shift(4'b0001), .out({SHR_out, right_shift_carry}));
  BarrelShifter #(.Bits(8), .barrelShifterMode("arithmetic"), .direction("right")) ASR (
    .in(multiplexer_8_out), .shift(4'b0001), .out(ASR_out));
  Multiplexer #(.Selector_Bits(2), .Bits(8)) multiplexer_10 (
    .sel(ShiftSelect), .in_0({left_shift_carry, SHL_out}), .in_1({SHR_out, right_shift_carry}),
    .in_2(ASR_out), .in_3(multiplexer_8_out), .out({left_sign, shift}));
  ROM #(.AddrBits(20), .Bits(8)) Logic_Unit (
    .A({LogicSelect, multiplexer_9_out, multiplexer_8_out}), .sel(1'b1), .D(\logic ));
  Multiplexer #(.Selector_Bits(2)) multiplexer_11 (
    .sel(CarrySelect), .in_0(1'b0), .in_1(add_carry), .in_2(right_shift_carry), .in_3(left_shift_carry),
    .out(carry));
  Register #(.Bits(8)) Offset_Register_2 (.D(DataBus), .C(Clk), .en(LoadOffset), .Q(off));
  Add #(.Bits(8)) add_1 (
    .a({left_sign, shift}), .b(\logic ), .c_i(multiplexer_12_out), .s({negative, result}), .c_o(add_carry));
  Register #(.Bits(4)) Bank_Register_2 (.D(DataBus[3:0]), .C(Clk), .en(LoadBR), .Q(br));
  and and_7 (and_7_out, Flags[1], nCodeAccess);
  Comparator #(.Bits(8)) comparator_1 (.a({negative, result}), .b({8{1'b0}}), .eq(NewAluFlags[2]));  // open: gt, lt
  Multiplexer #(.Selector_Bits(2)) multiplexer_12 (
    .sel(AdderSelect), .in_0(1'b0), .in_1(1'b1), .in_2(AluFlags[3]), .in_3(1'b0), .out(multiplexer_12_out));
  Multiplexer #(.Selector_Bits(2), .Bits(8)) multiplexer_13 (
    .sel(OffsetMode), .in_0({8{1'b0}}), .in_1(off), .in_2(8'h1), .in_3({8{1'b1}}), .out(multiplexer_13_out));
  // Probe Logic on \logic 
  // Probe Shift on {left_sign, shift}
  // Probe Result on {negative, result}
  Multiplexer #(.Selector_Bits(3)) multiplexer_14 (
    .sel({negative, left_sign, \logic [7]}), .in_0(1'b0), .in_1(1'b0), .in_2(1'b0), .in_3(1'b1), .in_4(1'b1),
    .in_5(1'b0), .in_6(1'b0), .in_7(1'b0), .out(NewAluFlags[1]));
  BitExtender bitextender_1 (.in(multiplexer_13_out), .out(bitextender_1_out));
  or or_6 (or_6_out, and_7_out, Flags[2]);
  Multiplexer #(.Bits(8)) multiplexer_15 (
    .sel(ResultSelect), .in_0({AluFlags, Flags}), .in_1({negative, result}), .out(multiplexer_15_out));
  // Probe on br
  // Probe on off
  Add #(.Bits(16)) add_2 (.a(bitextender_1_out), .b(multiplexer_7_out), .c_i(1'b0), .s(add_2_s));  // open: c_o
  Multiplexer #(.Bits(4)) multiplexer_16 (.sel(or_6_out), .in_0(4'b0000), .in_1(br), .out(multiplexer_16_out));
  Multiplexer #(.Bits(8)) multiplexer_17 (
    .sel(RegisterWriteBackSelect), .in_0(multiplexer_15_out), .in_1(mdi), .out(DataBus));
  Multiplexer #(.Selector_Bits(2)) multiplexer_18 (
    .sel(IrqEnableFlagControl), .in_0(Flags[0]), .in_1(Flags[0]), .in_2(1'b0), .in_3(1'b1), .out(NewIrqEnable));
  // Probe on mcr
  // Probe on mbr
  // Probe on mar
  D_FF #(.Bits(16)) Addr_Register (.D(add_2_s), .C(Clk), .Q(mar));  // open: nQ
  D_FF #(.Bits(4)) Bank_Register_3 (.D(multiplexer_16_out), .C(Clk), .Q(mbr));  // open: nQ
  D_FF #(.Bits(3)) Control_Register (.D({nCodeAccess, nIOAccess, Flags[2]}), .C(Clk), .Q(mcr));  // open: nQ
  D_FF #(.Bits(8)) Data_Register__In (.D(MemoryData), .C(Clk), .Q(mdi));  // open: nQ
  D_FF #(.Bits(8)) Data_Register__Out (.D(multiplexer_15_out), .C(Clk), .Q(mdo));  // open: nQ
  and and_8 (and_8_out, ~Flags[2], LoadFlags);  // And
  and and_9 (NewnKernel, ~EnterKernelMode, Flags[2]);  // And
  Multiplexer #(.Bits(8)) multiplexer_19 (
    .sel(and_8_out),
    .in_0({carry, NewAluFlags, negative, NewNmiActive, NewnKernel, NewUserData, NewIrqEnable}),
    .in_1(DataBus), .out(multiplexer_19_out));
  assign Address = AssertSystemBus ? mar : 16'bz;  // Driver driver_1
  assign Bank = AssertSystemBus ? mbr : 4'bz;  // Driver driver_2
  assign Control = AssertSystemBus ? mcr : 3'bz;  // Driver driver_3
  assign MemoryData = Write ? mdo : 8'bz;  // Driver driver_4
  reg8 reg8_1 (.D(multiplexer_19_out), .C(Clk), .en(1'b1), .clr(Rst_t), .Q({AluFlags, Flags}));
  or or_7 (NewNmiActive, SetNmiActive, Flags[3]);
  Multiplexer #(.Selector_Bits(2)) multiplexer_20 (
    .sel(UserDataFlagControl), .in_0(Flags[1]), .in_1(Flags[1]), .in_2(1'b0), .in_3(1'b1), .out(NewUserData));
  ROM #(.AddrBits(16), .Bits(8)) rom_1 (.A(Address), .sel(1'b1), .D(MemoryData));
  LED IrqEnable_2 (.in(Flags[0]));
  LED UserData_2 (.in(Flags[1]));
  LED nKernel_2 (.in(Flags[2]));
  LED NmiActive_2 (.in(Flags[3]));
  LED Sign_2 (.in(AluFlags[0]));
  LED Overflow_2 (.in(AluFlags[1]));
  LED Zero_2 (.in(AluFlags[2]));
  LED Carry_2 (.in(AluFlags[3]));

  // Other names for the same wires on the sheet: IrqEnable = Flags[0]; SysFlags[3:0] = Flags; UserData = Flags[1];
  //   nKernel = Flags[2]; NmiActive = Flags[3]; Flags[7:4] = AluFlags; SignFlag = AluFlags[0];
  //   OverflowFlag = AluFlags[1]; ZeroFlag = AluFlags[2]; CarryFlag = AluFlags[3];
  //   NewAluFlags (some bits) = {carry, negative}; right_sign = \logic [7]; overflow = NewAluFlags[1];
  //   result[7] = negative; shift[7] = left_sign; zero = NewAluFlags[2]

  // Notes on the sheet:
  //   _100_Hz: Hz: 100
  //   Control Unit
  //   Clock & Reset
  //   TODO: Generate ACK Signal.
  //   Just ~AssertSystemBus?
  //   ~brk
  //   (Synchronized)
  //   Mem/~IO  ^^^
  //   <<< NoClockPointerSelect
  //   Stored Values
  //   TODO: ResetSequencer should be negative to facilitate clearing extension bit
  //   Reset Logic
  //   - Asynchronous Activation?
  //   - Synchronous Deactivation?
  //   - Reset via IO?
  //   - Reset upon nested NMI.
  //   TODO: Encode SysFlags control lines
  //   FlagControl
  //   1 - ChangeFlag
  //   0 - NewValue
  //   InterruptMode
  //   ResetSequencer
  //   SequencerStep
  //   Pointer File
  //   Register File
  //   Address Generation Unit
  //   Arithmetic & Logic Unit
  //   contents of Logic_Unit (hex, n*v repeats v):
  //   5
  //   Status Flags
  //   Bank Register
  //   Offset Register
  //   .
  //   bw8 cpu rev2
  //   ***july 2023***
  //   8-bit WriteBack
  //   16-bit WriteBack
  //   Control Register
  //   Addr Register
  //   Only allow writes to Flags
  //   while in KernelMode
  //   Memory & IO
  //   contents of rom_1 (hex, n*v repeats v):
  //   5
endmodule
