// Digital circuit reg16.dig as structural Verilog
module reg16 (
  input  [15:0] D,
  input  C,
  input  EnL,
  input  EnH,
  input  clr,
  output [15:0] Q
);

  wire [15:0] multiplexer_1_out;

  Multiplexer #(.Bits(16)) multiplexer_1 (.sel(clr), .in_0(D), .in_1({16{1'b0}}), .out(multiplexer_1_out));
  Register #(.Bits(8), .isProgramCounter("true")) register_1 (.D(multiplexer_1_out[7:0]), .C(C), .en(EnL), .Q(Q[7:0]));
  Register #(.Bits(8), .isProgramCounter("true")) register_2 (
    .D(multiplexer_1_out[15:8]), .C(C), .en(EnH), .Q(Q[15:8]));
endmodule
