// Digital circuit reg8.dig as structural Verilog
module reg8 (
  input  [7:0] D,
  input  C,
  input  en,
  input  clr,
  output [7:0] Q
);

  wire [7:0] multiplexer_1_out;

  Multiplexer #(.Bits(8)) multiplexer_1 (.sel(clr), .in_0(D), .in_1({8{1'b0}}), .out(multiplexer_1_out));
  Register #(.Bits(8)) register_1 (.D(multiplexer_1_out), .C(C), .en(en), .Q(Q));
endmodule
